# Fritzing sketch leibniz (saved by Fritzing 0.9.3b)

parts:
  VCC1 = Battery  # not connected
  GY1 = MPU-6050 Board GY-521 [form="♀ (female)" package=THT]
  Деталь2 = 2A MOTOR SHIELD 9
  M1 = DC Motor
  M2 = DC Motor
  VCC2 = Battery
  Деталь3 = Arduino Pro Mini (5V)
  2_Channel_Relay1 = 2 Channel Power Relay
  Reg1 = DC-DC CONVERTER [part_number=80633 package=dc-dc_converter]
  TTP223B1 = TTP223B Capacitive Touch Sensor Module

nets:
  N1: GY1.pin1, Деталь2.3V3
  N2: GY1.pin2, Деталь2.GND#connector1pad-4-5-0-39-8-14
  N3: GY1.pin3, Деталь2.A5
  N4: GY1.pin4, Деталь2.A4
  N5: Деталь2.GND#0, Деталь3.RAW, 2_Channel_Relay1.K2-NC
  N6: Деталь2.PWRIN, Reg1.OUT-
  N7: Деталь2.VIN, 2_Channel_Relay1.K1-NC
  N8: Деталь2.M2+, M2.pin_1
  N9: Деталь2.M2-, M2.pin_2
  N10: Деталь2.M1+, M1.pin_1
  N11: Деталь2.M1-, M1.pin_2
  N12: VCC2.-, Reg1.IN-
  N13: VCC2.+, Reg1.IN+
  VCC: Деталь3.VCC, 2_Channel_Relay1.VCC, TTP223B1.VCC
  GND: Деталь3.GND, 2_Channel_Relay1.GND, TTP223B1.GND
  N14: Деталь3.D6, TTP223B1.SIG
  N15: Деталь3.D5, 2_Channel_Relay1.IN1
  N16: Деталь3.D3, 2_Channel_Relay1.IN2
  N17: 2_Channel_Relay1.K2-COM, Reg1.OUT+

custom parts:
  Battery: Your standard 2x 18650 battery pack (7,4 Volts)
  MPU-6050 Board GY-521: Acelerometro y Giroscopio MPU-6050 Board GY-521
  2 Channel Power Relay: A 2 channel power relay. The module operates at 5V.
  DC-DC CONVERTER: WYHP 5A constant current/voltage manufactured by Shenzhen Weiyapuhua Technology Co., Ltd
  TTP223B Capacitive Touch Sensor Module: The TTP223B capacitive touch sensor module uses the TTP223B IC. The appropriate voltage is approximately 2 to 5.5 volts.
